# Fritzing sketch Thermomter (saved by Fritzing 0.9.3b)
breadboards: 1

parts:
  U1 = NodeMCU V1.0
  Grove1 = Grove OLED 128x96
  Part1 = KY-015 Temperature & Humidity Sensor Module [package="Breakout board"]

nets:
  N1: U1.D1, Grove1.SCL
  N2: U1.D2, Grove1.SDA
  GND: U1.GND, Grove1.GND
  N3: U1.D5, Part1.Vin
  VIN: U1.Vin, Grove1.VCC, Part1.S, Part1.-

custom parts:
  NodeMCU V1.0: ESP8266 based NodeMCU
  KY-015 Temperature & Humidity Sensor Module: KY-015 temperature and humidity sensor module, provides a low-latency serial interface to measure humidity and temperature.
